// Logisim project cr8.circ as structural Verilog: 12 circuits, main circuit core
module main (
);

  wire and_1_out, and_2_out, and_3_out, and_4_out, and_5_out, and_6_out, and_7_out, and_8_out, CLK,
       comparator_2_eq, comparator_3_eq, comparator_4_eq, comparator_5_eq, core_1_dev_read, core_1_dev_write,
       core_1_dw_mem, ctrl_1_dr_dev, ctrl_1_dr_f, ctrl_1_dr_io, ctrl_1_dr_k, ctrl_1_dr_lhs, ctrl_1_dr_rhs,
       ctrl_1_dr_sel, ctrl_1_dw_sel, ctrl_1_pc_inc, ctrl_1_pc_jmp, ctrl_1_pc_jnz, ctrl_1_sp_dec,
       ctrl_1_sp_inc, decoder_1_out0, decoder_1_out1, decoder_1_out3, decoder_1_out4, decoder_1_out5,
       decoder_1_out6, decoder_1_out7, MEM_WE, SEL_BANK, SEL_RAM, SEL_ROM;
  wire [1:0] ctrl_1_aw;
  wire [2:0] ctrl_1_alu_op, ctrl_1_dw;
  wire [2:2] comparator_1_eq;
  wire [7:0] BANK, BANK_VRAM_dout, BUILTIN_RAM_dout, controlled_buffer_1_out, controlled_buffer_6_out,
       core_1_rio, ctrl_1_op, DB, DB_in, dev_kb_1_miso, dev_rng_1_miso, ram_1_dout, rom_1_data;
  wire [14:0] bit_extender_1_out;
  wire [15:0] AB;

  Clock clock_1 (.out(CLK));
  Comparator comparator_1 (.a(BANK), .b({8{1'b0}}), .eq(comparator_1_eq[2]));  // open: gt, lt
  Decoder #(.enable("false"), .select(3)) decoder_1 (
    .out0(decoder_1_out0), .out1(decoder_1_out1), .out2(SEL_BANK), .out3(decoder_1_out3),
    .out4(decoder_1_out4), .out5(decoder_1_out5), .out6(decoder_1_out6), .out7(decoder_1_out7),
    .sel({comparator_1_eq[2], AB[15:14]}));
  or or_1 (SEL_ROM, decoder_1_out0, decoder_1_out1, decoder_1_out4, decoder_1_out5);
  or or_2 (SEL_RAM, decoder_1_out6, decoder_1_out7, decoder_1_out3);
  Comparator comparator_2 (.a(BANK), .b(8'h1), .eq(comparator_2_eq));  // open: gt, lt
  Comparator comparator_3 (.a(BANK), .b(8'h2), .eq(comparator_3_eq));  // open: gt, lt
  ROM #(.addrWidth(15)) rom_1 (.addr(bit_extender_1_out), .data(rom_1_data));
  assign bit_extender_1_out = {{1{AB[14]}}, AB[13:0]};  // Bit_Extender bit_extender_1
  RAM #(.addrWidth(15), .enables("line")) BUILTIN_RAM (
    .addr(bit_extender_1_out), .we(and_1_out), .clk(CLK), .din(DB), .dout(BUILTIN_RAM_dout));
  and and_1 (and_1_out, SEL_RAM, MEM_WE);
  and and_2 (and_2_out, comparator_2_eq, SEL_BANK);
  RAM #(.addrWidth(14), .enables("line")) BANK_VRAM (
    .addr(AB[13:0]), .we(and_3_out), .clk(CLK), .din(DB), .dout(BANK_VRAM_dout));
  and and_3 (and_3_out, and_2_out, MEM_WE);
  and and_4 (and_4_out, comparator_3_eq, SEL_BANK);
  RAM #(.addrWidth(14), .enables("line")) ram_1 (
    .addr(AB[13:0]), .we(and_5_out), .clk(CLK), .din(DB), .dout(ram_1_dout));
  and and_5 (and_5_out, and_4_out, MEM_WE);
  assign controlled_buffer_1_out = SEL_ROM ? rom_1_data : 8'bz;  // Controlled_Buffer controlled_buffer_1
  assign controlled_buffer_1_out = SEL_RAM ? BUILTIN_RAM_dout : 8'bz;  // Controlled_Buffer controlled_buffer_2
  assign controlled_buffer_1_out = and_2_out ? BANK_VRAM_dout : 8'bz;  // Controlled_Buffer controlled_buffer_3
  assign controlled_buffer_1_out = and_4_out ? ram_1_dout : 8'bz;  // Controlled_Buffer controlled_buffer_4
  core core_1 (
    .DW(ctrl_1_dw), .AW(ctrl_1_aw), .CLK(CLK), .DR_K(ctrl_1_dr_k), .DR_F(ctrl_1_dr_f), .DR_IO(ctrl_1_dr_io),
    .DR_LHS(ctrl_1_dr_lhs), .DR_RHS(ctrl_1_dr_rhs), .DR_DEV(ctrl_1_dr_dev), .DR_SEL(ctrl_1_dr_sel),
    .DW_SEL(ctrl_1_dw_sel), .PC_JNZ(ctrl_1_pc_jnz), .PC_J(ctrl_1_pc_jmp), .PC_INC(ctrl_1_pc_inc),
    .ALU_OP(ctrl_1_alu_op), .SP_INC(ctrl_1_sp_inc), .SP_DEC(ctrl_1_sp_dec), .RST(1'b0), .OP(ctrl_1_op),
    .DB_in(DB_in), .rIO(core_1_rio), .DEV_WRITE(core_1_dev_write), .DEV_READ(core_1_dev_read),
    .DW_MEM(core_1_dw_mem), .DATA(DB), .rK(BANK), .ADDR(AB));
  ctrl ctrl_1 (
    .MEM(controlled_buffer_1_out), .CLK(CLK), .RST(1'b0), .SP_DEC(ctrl_1_sp_dec), .SP_INC(ctrl_1_sp_inc),
    .PC_JMP(ctrl_1_pc_jmp), .DR_DEV(ctrl_1_dr_dev), .DR_MEM(MEM_WE), .DR_IO(ctrl_1_dr_io),
    .DR_F(ctrl_1_dr_f), .DR_K(ctrl_1_dr_k), .PC_JNZ(ctrl_1_pc_jnz), .DW_SEL(ctrl_1_dw_sel),
    .DR_SEL(ctrl_1_dr_sel), .ALU_OP(ctrl_1_alu_op), .AW(ctrl_1_aw), .DW(ctrl_1_dw), .PC_INC(ctrl_1_pc_inc),
    .DR_LHS(ctrl_1_dr_lhs), .DR_RHS(ctrl_1_dr_rhs), .OP(ctrl_1_op));
  assign DB_in = core_1_dw_mem ? controlled_buffer_1_out : 8'bz;  // Controlled_Buffer controlled_buffer_5
  assign controlled_buffer_6_out = and_6_out ? DB : 8'bz;  // Controlled_Buffer controlled_buffer_6
  Comparator comparator_4 (.a(core_1_rio), .b(8'h1), .eq(comparator_4_eq));  // open: gt, lt
  and and_6 (and_6_out, core_1_dev_read, comparator_4_eq);
  and and_7 (and_7_out, comparator_4_eq, core_1_dev_write);
  dev_kb dev_kb_1 (.CLK(CLK), .SEND(and_7_out), .RECV(and_6_out), .MOSI(controlled_buffer_6_out), .MISO(dev_kb_1_miso));
  assign DB_in = and_7_out ? dev_kb_1_miso : 8'bz;  // Controlled_Buffer controlled_buffer_7
  Comparator comparator_5 (.a(core_1_rio), .b(8'h2), .eq(comparator_5_eq));  // open: gt, lt
  and and_8 (and_8_out, comparator_5_eq, core_1_dev_write);
  assign DB_in = and_8_out ? dev_rng_1_miso : 8'bz;  // Controlled_Buffer controlled_buffer_8
  dev_rng dev_rng_1 (.CLK(CLK), .MISO(dev_rng_1_miso));

  // Notes on the sheet:
  //   contents of rom_1 (hex, n*v repeats v):
  //   8 3 9 3e 90 1
endmodule

module core (
  input  CLK,
  input  [2:0] DW,
  input  [1:0] AW,
  input  [7:0] DB_in,
  input  DR_K,
  input  DR_F,
  input  DR_IO,
  input  DR_LHS,
  input  DR_RHS,
  input  [7:0] OP,
  input  DR_DEV,
  input  DR_SEL,
  input  DW_SEL,
  input  PC_JNZ,
  input  PC_J,
  input  PC_INC,
  input  [2:0] ALU_OP,
  input  SP_INC,
  input  SP_DEC,
  input  RST,
  output [7:0] DATA,
  output [15:0] ADDR,
  output DW_MEM,
  output [7:0] rK,
  output [7:0] rIO,
  output DEV_WRITE,
  output DEV_READ
);

  wire ALU_SEL_A, ALU_SEL_B, ALU_SEL_C, ALU_SEL_D, ALU_SEL_F, ALU_SEL_X, ALU_SEL_Y, ALU_SEL_Z, and_1_out,
       AR_PC, AW_LR, AW_PC, AW_SP, AW_XY, demultiplexer_1_out7, demultiplexer_6_out0, demultiplexer_6_out1,
       demultiplexer_6_out2, demultiplexer_6_out3, demultiplexer_6_out4, demultiplexer_6_out5,
       demultiplexer_6_out6, demultiplexer_6_out7, demultiplexer_7_out0, demultiplexer_7_out1,
       demultiplexer_7_out2, demultiplexer_7_out3, demultiplexer_7_out4, demultiplexer_7_out5,
       demultiplexer_7_out6, DR_A, DR_B, DR_C, DR_D, DR_F_t, DR_MEM, DR_X, DR_Y, DR_Z, DW_A, DW_AF, DW_ALU,
       DW_B, DW_C, DW_D, DW_F, DW_IO, DW_K, DW_OP, DW_RHS, DW_X, DW_Y, DW_Z, not_1_out, not_2_out, not_3_out,
       or_3_out;
  wire [2:0] DR, DW_t;
  wire [7:0] A_q, alu_1_f, alu_1_q, ALUB, B_q, C_q, D_q, F_q, X_q, Y_q, Z_q;
  wire [7:3] LHS_q;
  wire [9:0] SP_q;
  wire [15:0] PC_q;
  wire [15:11] RHS_q;

  Demultiplexer #(.select(3)) demultiplexer_1 (
    .out0(DR_A), .out1(DR_B), .out2(DR_C), .out3(DR_D), .out4(DR_X), .out5(DR_Y), .out6(DR_Z),
    .out7(demultiplexer_1_out7), .in(DR_SEL), .sel(DR));
  Demultiplexer #(.select(3)) demultiplexer_2 (
    .out0(ALU_SEL_A), .out1(ALU_SEL_B), .out2(ALU_SEL_C), .out3(ALU_SEL_D), .out4(ALU_SEL_X),
    .out5(ALU_SEL_Y), .out6(ALU_SEL_Z), .out7(ALU_SEL_F), .in(1'b1), .sel(DR));
  Demultiplexer #(.select(3)) demultiplexer_3 (
    .out0(DW_A), .out1(DW_B), .out2(DW_C), .out3(DW_D), .out4(DW_X), .out5(DW_Y), .out6(DW_Z), .out7(DW_F),
    .in(DW_SEL), .sel(DW_t));
  Demultiplexer #(.select(2)) demultiplexer_4 (
    .out0(AW_PC), .out1(AW_SP), .out2(AW_XY), .out3(AW_LR), .in(1'b1), .sel(AW));
  not not_1 (not_1_out, DW_SEL);
  Demultiplexer #(.select(3)) demultiplexer_5 (
    .out0(DW_MEM), .out1(DW_OP), .out2(DW_ALU), .out3(DW_AF), .out4(DW_K), .out5(DW_IO), .out6(DEV_WRITE),
    .out7(DW_RHS), .in(not_1_out), .sel(DW));
  or or_1 (DR_F_t, demultiplexer_1_out7, DR_F);
  assign DB_in = DW_OP ? OP : 8'bz;  // Controlled_Buffer controlled_buffer_1
  Demultiplexer #(.select(3)) demultiplexer_6 (
    .out0(demultiplexer_6_out0), .out1(demultiplexer_6_out1), .out2(demultiplexer_6_out2),
    .out3(demultiplexer_6_out3), .out4(demultiplexer_6_out4), .out5(demultiplexer_6_out5),
    .out6(demultiplexer_6_out6), .out7(demultiplexer_6_out7), .in(1'b1), .sel(OP[2:0]));
  LED led_1 (.in(OP[3]));
  LED led_2 (.in(demultiplexer_6_out0));
  LED led_3 (.in(demultiplexer_6_out1));
  LED led_4 (.in(demultiplexer_6_out2));
  LED led_5 (.in(demultiplexer_6_out3));
  LED led_6 (.in(demultiplexer_6_out4));
  LED led_7 (.in(demultiplexer_6_out5));
  LED led_8 (.in(demultiplexer_6_out6));
  LED led_9 (.in(demultiplexer_6_out7));
  Hex_Digit_Display hex_digit_display_1 (.value(OP[7:4]));  // open: dp
  LED led_10 (.in(AW_PC));
  LED led_11 (.in(AW_SP));
  LED led_12 (.in(AW_XY));
  LED led_13 (.in(AW_LR));
  LED led_14 (.in(DW_OP));
  LED led_15 (.in(DW_ALU));
  LED led_16 (.in(DW_AF));
  LED led_17 (.in(DW_K));
  LED led_18 (.in(DW_IO));
  LED led_19 (.in(DEV_WRITE));
  LED led_20 (.in(DW_RHS));
  LED led_21 (.in(DW_A));
  LED led_22 (.in(DW_B));
  LED led_23 (.in(DW_C));
  LED led_24 (.in(DW_D));
  LED led_25 (.in(DW_X));
  LED led_26 (.in(DW_Y));
  LED led_27 (.in(DW_Z));
  LED led_28 (.in(DW_F));
  LED led_29 (.in(DR_A));
  LED led_30 (.in(DR_B));
  LED led_31 (.in(DR_C));
  LED led_32 (.in(DR_D));
  LED led_33 (.in(DR_X));
  LED led_34 (.in(DR_Y));
  LED led_35 (.in(DR_Z));
  LED led_36 (.in(DR_F_t));
  LED led_37 (.in(DR_K));
  LED led_38 (.in(DR_IO));
  LED led_39 (.in(DR_MEM));
  LED led_40 (.in(DR_LHS));
  LED led_41 (.in(DR_RHS));
  LED led_42 (.in(DR_DEV));
  Register F (.D(DB_in), .en(DR_F_t), .clk(CLK), .Q(F_q), .clr(RST));
  byte_display byte_display_1 (.in_1(DB_in));
  Register A (.D(DB_in), .en(DR_A), .clk(CLK), .Q(A_q), .clr(RST));
  Register K (.D(DB_in), .en(DR_K), .clk(CLK), .Q(rK), .clr(RST));
  Register LHS (.D(DB_in), .en(DR_LHS), .clk(CLK), .Q({LHS_q, DR}), .clr(RST));
  byte_display byte_display_2 (.in_1(F_q));
  byte_display byte_display_3 (.in_1(A_q));
  assign DB_in = DW_A ? A_q : 8'bz;  // Controlled_Buffer controlled_buffer_2
  assign ALUB = ALU_SEL_A ? A_q : 8'bz;  // Controlled_Buffer controlled_buffer_3
  byte_display byte_display_4 (.in_1(rK));
  assign DB_in = DW_K ? rK : 8'bz;  // Controlled_Buffer controlled_buffer_4
  byte_display byte_display_5 (.in_1({LHS_q, DR}));
  assign DB_in = DW_F ? F_q : 8'bz;  // Controlled_Buffer controlled_buffer_5
  LED led_43 (.in(F_q[0]));
  LED led_44 (.in(F_q[1]));
  LED led_45 (.in(F_q[2]));
  LED led_46 (.in(F_q[3]));
  LED led_47 (.in(F_q[4]));
  Demultiplexer #(.select(3)) demultiplexer_7 (
    .out0(demultiplexer_7_out0), .out1(demultiplexer_7_out1), .out2(demultiplexer_7_out2),
    .out3(demultiplexer_7_out3), .out4(demultiplexer_7_out4), .out5(demultiplexer_7_out5),
    .out6(demultiplexer_7_out6), .in(1'b1), .sel(ALU_OP));  // open: out7
  assign ADDR = AW_LR ? {RHS_q, DW_t, LHS_q, DR} : 16'bz;  // Controlled_Buffer controlled_buffer_6
  LED led_48 (.in(ALU_SEL_A));
  LED led_49 (.in(ALU_SEL_B));
  LED led_50 (.in(ALU_SEL_C));
  LED led_51 (.in(ALU_SEL_D));
  LED led_52 (.in(ALU_SEL_X));
  LED led_53 (.in(ALU_SEL_Y));
  LED led_54 (.in(ALU_SEL_Z));
  LED led_55 (.in(ALU_SEL_F));
  LED led_56 (.in(demultiplexer_7_out0));
  LED led_57 (.in(demultiplexer_7_out1));
  LED led_58 (.in(demultiplexer_7_out2));
  LED led_59 (.in(demultiplexer_7_out3));
  LED led_60 (.in(demultiplexer_7_out4));
  LED led_61 (.in(demultiplexer_7_out5));
  LED led_62 (.in(demultiplexer_7_out6));
  LED led_63 (.in(PC_JNZ));
  LED led_64 (.in(PC_J));
  LED led_65 (.in(PC_INC));
  LED led_66 (.in(SP_INC));
  LED led_67 (.in(SP_DEC));
  addr_display addr_display_1 (.in_1(ADDR));
  Register B (.D(DB_in), .en(DR_B), .clk(CLK), .Q(B_q), .clr(RST));
  Register X (.D(DB_in), .en(DR_X), .clk(CLK), .Q(X_q), .clr(RST));
  Register RHS (.D(DB_in), .en(DR_RHS), .clk(CLK), .Q({RHS_q, DW_t}), .clr(RST));
  assign DB_in = DW_ALU ? alu_1_q : 8'bz;  // Controlled_Buffer controlled_buffer_7
  byte_display byte_display_6 (.in_1(B_q));
  assign DB_in = DW_B ? B_q : 8'bz;  // Controlled_Buffer controlled_buffer_8
  assign ALUB = ALU_SEL_B ? B_q : 8'bz;  // Controlled_Buffer controlled_buffer_9
  byte_display byte_display_7 (.in_1(X_q));
  assign DB_in = DW_X ? X_q : 8'bz;  // Controlled_Buffer controlled_buffer_10
  assign ALUB = ALU_SEL_X ? X_q : 8'bz;  // Controlled_Buffer controlled_buffer_11
  assign ADDR = AW_XY ? {Y_q, X_q} : 16'bz;  // Controlled_Buffer controlled_buffer_12
  byte_display byte_display_8 (.in_1({RHS_q, DW_t}));
  assign DB_in = DW_RHS ? {RHS_q, DW_t} : 8'bz;  // Controlled_Buffer controlled_buffer_13
  alu alu_1 (.B({RHS_q, DW_t}), .A(ALUB), .OP(ALU_OP), .F_in(F_q), .Q(alu_1_q), .F(alu_1_f));
  Register C (.D(DB_in), .en(DR_C), .clk(CLK), .Q(C_q), .clr(RST));
  Register Y (.D(DB_in), .en(DR_Y), .clk(CLK), .Q(Y_q), .clr(RST));
  assign DB_in = DW_AF ? alu_1_f : 8'bz;  // Controlled_Buffer controlled_buffer_14
  not not_2 (not_2_out, alu_1_f[5]);
  and and_1 (and_1_out, not_2_out, PC_JNZ);
  byte_display byte_display_9 (.in_1(C_q));
  byte_display byte_display_10 (.in_1(Y_q));
  Register IO (.D(DB_in), .en(DR_IO), .clk(CLK), .Q(rIO), .clr(RST));
  or or_2 (AR_PC, and_1_out, PC_J);
  assign DB_in = DW_C ? C_q : 8'bz;  // Controlled_Buffer controlled_buffer_15
  assign ALUB = ALU_SEL_C ? C_q : 8'bz;  // Controlled_Buffer controlled_buffer_16
  assign DB_in = DW_Y ? Y_q : 8'bz;  // Controlled_Buffer controlled_buffer_17
  assign ALUB = ALU_SEL_Y ? Y_q : 8'bz;  // Controlled_Buffer controlled_buffer_18
  byte_display byte_display_11 (.in_1(rIO));
  Register D (.D(DB_in), .en(DR_D), .clk(CLK), .Q(D_q), .clr(RST));
  Register Z (.D(DB_in), .en(DR_Z), .clk(CLK), .Q(Z_q), .clr(RST));
  assign DB_in = DW_IO ? rIO : 8'bz;  // Controlled_Buffer controlled_buffer_19
  byte_display byte_display_12 (.in_1(D_q));
  assign DB_in = DW_D ? D_q : 8'bz;  // Controlled_Buffer controlled_buffer_20
  assign ALUB = ALU_SEL_D ? D_q : 8'bz;  // Controlled_Buffer controlled_buffer_21
  byte_display byte_display_13 (.in_1(Z_q));
  assign DB_in = DW_Z ? Z_q : 8'bz;  // Controlled_Buffer controlled_buffer_22
  assign ALUB = ALU_SEL_Z ? Z_q : 8'bz;  // Controlled_Buffer controlled_buffer_23
  Counter #(.max('hffff), .width(16)) PC (
    .clr(RST), .load(AR_PC), .up(1'b1), .count(PC_INC), .clk(CLK), .D(ADDR), .Q(PC_q));  // open: carry
  addr_display addr_display_2 (.in_1(PC_q));
  assign ADDR = AW_PC ? PC_q : 16'bz;  // Controlled_Buffer controlled_buffer_24
  Counter #(.max('h2ff), .width(10)) SP (
    .clr(RST), .up(not_3_out), .count(or_3_out), .clk(CLK), .D(ADDR[9:0]), .Q(SP_q));  // open: load, carry
  not not_3 (not_3_out, SP_DEC);
  or or_3 (or_3_out, SP_DEC, SP_INC);
  addr_display addr_display_3 (.in_1({{6{1'b1}}, SP_q}));
  assign ADDR = AW_SP ? {{6{1'b1}}, SP_q} : 16'bz;  // Controlled_Buffer controlled_buffer_25

  assign DATA = DB_in;
  assign DEV_READ = DR_DEV;

  // Other names for the same wires on the sheet: AB[15:0] = ADDR; ADDRBUS_WRITER[1:0] = AW; DATABUS_WRITER[2:0] = DW;
  //   DB[7:0] = DB_in; DW_DEV = DEV_WRITE; PCJMP = PC_J; PCJNZ = PC_JNZ

  // Notes on the sheet:
  //   DATA BUS
  //   ADDRESS BUS
endmodule

module ctrl (
  input  [7:0] MEM,
  input  RST,
  input  CLK,
  output [7:0] OP,
  output DR_DEV,
  output DR_MEM,
  output DR_IO,
  output DR_F,
  output DR_LHS,
  output DR_K,
  output DR_RHS,
  output PC_JNZ,
  output [1:0] AW,
  output [2:0] DW,
  output DW_SEL,
  output DR_SEL,
  output SP_DEC,
  output SP_INC,
  output [2:0] ALU_OP,
  output PC_INC,
  output PC_JMP
);

  wire and_1_out, and_2_out, and_3_out, and_4_out, and_5_out, and_6_out, and_7_out, and_8_out, and_9_out,
       and_10_out, and_11_out, nor_1_out, not_1_out, not_2_out, not_3_out, not_4_out, not_5_out, or_2_out,
       or_3_out;
  wire [2:0] counter_1_q;
  wire [5:1] R0_data;
  wire [6:0] R2_data;

  Register rOP (.D(MEM), .en(nor_1_out), .clk(CLK), .Q(OP), .clr(RST));
  Counter #(.max('h7), .width(3)) counter_1 (
    .clr(RST), .load(R2_data[0]), .up(1'b1), .count(1'b1), .clk(CLK), .D(3'b000), .Q(counter_1_q));  // open: carry
  Hex_Digit_Display #(.decimalPoint("false")) hex_digit_display_1 (.value({1'b0, counter_1_q}));
  ROM R0 (.addr({OP[7:3], counter_1_q}), .data({DR_K, DR_F, R0_data[5], DR_IO, DR_MEM, R0_data[2:1], DR_DEV}));
  ROM R1 (.addr({OP[7:3], counter_1_q}), .data({DR_SEL, DW_SEL, DW, AW, PC_JNZ}));
  ROM R2 (.addr({OP[7:3], counter_1_q}), .data({PC_JMP, R2_data[6], ALU_OP, SP_INC, SP_DEC, R2_data[0]}));
  nor nor_1 (nor_1_out, counter_1_q[0], counter_1_q[1], counter_1_q[2]);
  or or_1 (PC_INC, R2_data[6], nor_1_out);
  not not_1 (not_1_out, OP[3]);
  not not_2 (not_2_out, OP[4]);
  not not_3 (not_3_out, OP[5]);
  not not_4 (not_4_out, OP[6]);
  not not_5 (not_5_out, OP[7]);
  and and_1 (and_1_out, not_5_out, OP[6], OP[4]);
  and and_2 (and_2_out, not_5_out, OP[6], not_3_out, not_2_out);
  or or_2 (or_2_out, and_1_out, and_2_out, and_3_out);
  and and_3 (and_3_out, not_1_out, OP[4], OP[5], OP[6]);
  and and_4 (and_4_out, not_4_out, not_3_out);
  and and_5 (and_5_out, not_3_out, OP[4]);
  and and_6 (and_6_out, OP[6], OP[5], not_2_out);
  and and_7 (and_7_out, OP[7], not_4_out);
  and and_8 (and_8_out, not_4_out, not_2_out, OP[3]);
  and and_9 (and_9_out, not_2_out, OP[7]);
  or or_3 (or_3_out, and_4_out, and_5_out, and_6_out, and_7_out, and_8_out, and_9_out);
  or or_4 (DR_LHS, R0_data[2], and_10_out);
  and and_10 (and_10_out, or_3_out, nor_1_out);
  and and_11 (and_11_out, nor_1_out, or_2_out);
  or or_5 (DR_RHS, and_11_out, R0_data[1]);

  // Notes on the sheet:
  //   contents of R0 (hex, n*v repeats v):
  //   0 2 15*0 2 40 6*0 40 4 2 13*0 4 2 14*0 4 2 2 4 4*0 8 7*0 10 4 2 8 4*0 8 7*0 8 23*0 2 10 6*0 10 7*0
  //   10 2 1 5*0 10 1 6*0 2 2 10 40 4*0 2 10 40 5*0 2 2 10 40 4*0 2 10 40 5*0 2 2 40 5*0 2 40 6*0 2 2 10
  //   40 4*0 2 10 40 5*0 2 2 10 40 4*0 2 10 40 5*0 2 2 10 40 4*0 10 40 6*0 80 7*0 80
  //   contents of R1 (hex, n*v repeats v):
  //   0 0 c0 6*0 80 8*0 18 5 5*0 18 0 0 7 4*0 4 9*0 6 5*0 84 9*0 6 8 b8 0 0 0 44 7*0 40 0 0 2e 4*0 42 7*0
  //   3a 8*0 82 15*0 40 b0 6*0 b0 6*0 40 0 40 5*0 40 8*0 40 10 18 a8 4*0 10 18 a8 5*0 40 10 18 a8 4*0 10
  //   18 a8 5*0 40 18 6*0 18 7*0 40 10 18 a8 4*0 10 18 a8 5*0 40 10 18 a8 4*0 10 18 a8 5*0 40 10 18 a8 0 0
  //   0 10 18 a8 5*0 40
  //   contents of R2 (hex, n*v repeats v):
  //   0 0 41 5*1 0 41 6*1 0 40 30 5*1 0 30 40 40 4*1 0 81 6*1 0 40 40 81 4*1 0 41 6*1 0 40 40 0 0 1 1 1 0
  //   7*1 0 0 40 0 41 1 1 1 0 5 6*1 0 5 6*1 0 2 6*1 9*0 40 0 5*1 0 40 6*1 0 40 40 5*1 0 40 41 5*1 0 40 0 0
  //   0 1 1 1 0 40 0 0 4*1 0 40 0 8 8 1 1 1 0 40 8 8 4*1 0 40 0 31 4*1 0 40 31 5*1 0 40 0 20 20 1 1 1 0 40
  //   20 20 4*1 0 40 0 10 10 1 1 1 0 40 10 10 4*1 0 40 0 18 18 1 1 1 0 18 18 5*1 0 41 6*1 0 41 6*1
endmodule

module alu (
  input  [2:0] OP,
  input  [7:0] F_in,
  input  [7:0] A,
  input  [7:0] B,
  output [7:0] F,
  output [7:0] Q
);

  wire ad0_p1, ad1_p1, ad2_p1, bd0_p1, bd1_p1, bd2_p1, C, C_in, INV_B, INV_Q, multiplexer_2_out, not_1_out,
       not_2_out, not_3_out, not_4_out, op_add, op_and, op_cmp, op_nand, op_nor, op_or, op_sub, or_2_out,
       qd0_p1, qd1_p1, qd2_p1, Z;
  wire [7:0] adder_1_out, and_1_out, multiplexer_1_out, or_1_out, xor_1_out;

  xor xor_1 (xor_1_out[0], B[0], INV_B);
  xor xor_2 (xor_1_out[1], B[1], INV_B);
  xor xor_3 (xor_1_out[2], B[2], INV_B);
  xor xor_4 (xor_1_out[3], B[3], INV_B);
  xor xor_5 (xor_1_out[4], B[4], INV_B);
  xor xor_6 (xor_1_out[5], B[5], INV_B);
  xor xor_7 (xor_1_out[6], B[6], INV_B);
  xor xor_8 (xor_1_out[7], B[7], INV_B);
  assign or_1_out = A | xor_1_out;  // OR_Gate or_1, 8 bits wide
  assign and_1_out = A & xor_1_out;  // AND_Gate and_1, 8 bits wide
  Adder adder_1 (.a(A), .b(xor_1_out), .out(adder_1_out), .cin(C_in), .cout(C));
  Multiplexer #(.select(2), .width(8)) multiplexer_1 (
    .in0(adder_1_out), .in1(or_1_out), .in2(and_1_out), .in3(A), .out(multiplexer_1_out), .sel(OP[2:1]));
  Demultiplexer #(.select(3)) demultiplexer_1 (
    .out0(op_add), .out1(op_sub), .out2(op_or), .out3(op_nor), .out4(op_and), .out5(op_nand), .out6(op_cmp),
    .in(1'b1), .sel(OP));  // open: out7
  xor xor_9 (Q[0], multiplexer_1_out[0], INV_Q);
  xor xor_10 (Q[1], multiplexer_1_out[1], INV_Q);
  xor xor_11 (Q[2], multiplexer_1_out[2], INV_Q);
  xor xor_12 (Q[3], multiplexer_1_out[3], INV_Q);
  xor xor_13 (Q[4], multiplexer_1_out[4], INV_Q);
  xor xor_14 (Q[5], multiplexer_1_out[5], INV_Q);
  xor xor_15 (Q[6], multiplexer_1_out[6], INV_Q);
  xor xor_16 (Q[7], multiplexer_1_out[7], INV_Q);
  nor nor_1 (Z, Q[0], Q[1], Q[2], Q[3], Q[5], Q[6], Q[7], Q[4]);
  // _7_Segment_Display qd2: pin names not known; wires that end beside it: qd2_p1, qd2_p1
  // BCD_to_7_Segment_decoder bcd_to_7_segment_decoder_1: pin names not known
  Multiplexer multiplexer_2 (.in0(F_in[2]), .in1(not_1_out), .out(multiplexer_2_out), .sel(op_sub));
  not not_1 (not_1_out, F_in[3]);
  Multiplexer multiplexer_3 (.in0(F_in[2]), .in1(C), .out(F[2]), .sel(op_add));
  Multiplexer multiplexer_4 (.in0(F_in[3]), .in1(not_2_out), .out(F[3]), .sel(op_sub));
  not not_2 (not_2_out, C);
  Multiplexer multiplexer_5 (.in0(F_in[1]), .in1(not_3_out), .out(F[1]), .sel(op_cmp));
  not not_3 (not_3_out, C);
  Multiplexer multiplexer_6 (.in0(F_in[0]), .in1(Z), .out(F[0]), .sel(op_cmp));
  Multiplexer multiplexer_7 (.in0(F_in[4]), .in1(Z), .out(F[4]), .sel(or_2_out));
  or or_2 (or_2_out, op_sub, op_add);
  // _7_Segment_Display qd1: pin names not known; wires that end beside it: qd1_p1, qd1_p1
  // BCD_to_7_Segment_decoder bcd_to_7_segment_decoder_2: pin names not known
  // Binary_to_BCD_converter #(.binvalue(8)) binary_to_bcd_converter_1: pin names not known; wires that end beside it: Q
  or or_3 (INV_Q, op_nor, op_nand);
  or or_4 (INV_B, op_sub, op_cmp);
  not not_4 (not_4_out, op_cmp);
  and and_2 (C_in, not_4_out, multiplexer_2_out);
  // _7_Segment_Display qd0: pin names not known; wires that end beside it: qd0_p1, qd0_p1
  // BCD_to_7_Segment_decoder bcd_to_7_segment_decoder_3: pin names not known
  // _7_Segment_Display ad2: pin names not known; wires that end beside it: ad2_p1, ad2_p1
  // BCD_to_7_Segment_decoder bcd_to_7_segment_decoder_4: pin names not known
  // Binary_to_BCD_converter #(.binvalue(8)) binary_to_bcd_converter_2: pin names not known; wires that end beside it: A
  // _7_Segment_Display bd2: pin names not known; wires that end beside it: bd2_p1, bd2_p1
  // BCD_to_7_Segment_decoder bcd_to_7_segment_decoder_5: pin names not known
  // Binary_to_BCD_converter #(.binvalue(8)) binary_to_bcd_converter_3: pin names not known; wires that end beside it: B
  // _7_Segment_Display ad1: pin names not known; wires that end beside it: ad1_p1, ad1_p1
  // BCD_to_7_Segment_decoder bcd_to_7_segment_decoder_6: pin names not known
  // _7_Segment_Display bd1: pin names not known; wires that end beside it: bd1_p1, bd1_p1
  // BCD_to_7_Segment_decoder bcd_to_7_segment_decoder_7: pin names not known
  // _7_Segment_Display ad0: pin names not known; wires that end beside it: ad0_p1, ad0_p1
  // BCD_to_7_Segment_decoder bcd_to_7_segment_decoder_8: pin names not known
  // _7_Segment_Display bd0: pin names not known; wires that end beside it: bd0_p1, bd0_p1
  // BCD_to_7_Segment_decoder bcd_to_7_segment_decoder_9: pin names not known

  assign F[7:5] = F_in[7:5];

  // Other names for the same wires on the sheet: P_1 = OP[1]; P_2 = OP[2]; EF = F[0]; LF = F[1]; CF = F[2]; BF = F[3];
  //   ZF = F[4]; F_E = F_in[0]; F_L = F_in[1]; F_C = F_in[2]; F_B = F_in[3]; F_Z = F_in[4]; P_0 = OP[0]
endmodule

module dev_kb (
  input  CLK,
  input  SEND,
  input  RECV,
  input  [7:0] MOSI,
  output [7:0] MISO
);

  wire keyboard_1_avail;

  Keyboard keyboard_1 (.clk(CLK), .re(SEND), .clr(RECV), .avail(keyboard_1_avail), .data(MISO[6:0]));
  not not_1 (MISO[7], keyboard_1_avail);
endmodule

module dev_rng (
  input  CLK,
  output [7:0] MISO
);

  wire xor_1_out, xor_2_out;

  D_Flip_Flop d_ff_1 (.D(xor_2_out), .clk(CLK), .Q(MISO[0]));  // open: Qn, preset, reset
  D_Flip_Flop d_ff_2 (.D(MISO[0]), .clk(CLK), .Q(MISO[1]));  // open: Qn, preset, reset
  D_Flip_Flop d_ff_3 (.D(MISO[1]), .clk(CLK), .Q(MISO[2]));  // open: Qn, preset, reset
  D_Flip_Flop d_ff_4 (.D(MISO[2]), .clk(CLK), .Q(MISO[3]));  // open: Qn, preset, reset
  D_Flip_Flop d_ff_5 (.D(MISO[3]), .clk(CLK), .Q(MISO[4]));  // open: Qn, preset, reset
  D_Flip_Flop d_ff_6 (.D(MISO[4]), .clk(CLK), .Q(MISO[5]));  // open: Qn, preset, reset
  D_Flip_Flop d_ff_7 (.D(MISO[5]), .clk(CLK), .Q(MISO[6]));  // open: Qn, preset, reset
  D_Flip_Flop d_ff_8 (.D(MISO[6]), .clk(CLK), .Q(MISO[7]));  // open: Qn, preset, reset
  xor xor_1 (xor_1_out, MISO[7], 1'b1);
  xor xor_2 (xor_2_out, MISO[6], xor_1_out);
endmodule

module icreg (
);

  wire CLK, D0, D1, D2, D3, D4, D5, D6, D7, n74245_1_pin1, nRE, nWE, Q0, Q1, Q2, Q3, Q4, Q5, Q6, Q7;

  _74377 #(.ShowInternalStructure("true")) u_74377_1 (
    .pin1(nRE), .pin2(Q0), .pin3(D0), .pin4(D1), .pin5(Q1), .pin6(Q2), .pin7(D2), .pin8(D3), .pin9(Q3),
    .pin19(Q7), .pin18(D7), .pin17(D6), .pin16(Q6), .pin15(Q5), .pin14(D5), .pin13(D4), .pin12(Q4),
    .pin11(CLK));
  _74245 #(.ShowInternalStructure("true")) u_74245_1 (
    .pin1(n74245_1_pin1), .pin2(Q0), .pin3(Q1), .pin4(Q2), .pin5(Q3), .pin6(Q4), .pin7(Q5), .pin8(Q6),
    .pin9(Q7), .pin19(nWE), .pin18(D0), .pin17(D1), .pin16(D2), .pin15(D3), .pin14(D4), .pin13(D5),
    .pin12(D6), .pin11(D7));
  // also tied to VCC on the sheet: n74245_1_pin1
endmodule

module byte_display (
  input  [7:0] in_1
);

  wire d0_p1, d1_p1, d2_p1;

  // _7_Segment_Display d2: pin names not known; wires that end beside it: d2_p1, d2_p1
  // _7_Segment_Display d1: pin names not known; wires that end beside it: d1_p1, d1_p1
  // BCD_to_7_Segment_decoder bcd_to_7_segment_decoder_1: pin names not known
  // BCD_to_7_Segment_decoder bcd_to_7_segment_decoder_2: pin names not known
  // Binary_to_BCD_converter #(.binvalue(8)) binary_to_bcd_converter_1: pin names not known; wires that end beside it: in_1
  // _7_Segment_Display d0: pin names not known; wires that end beside it: d0_p1, d0_p1
  // BCD_to_7_Segment_decoder bcd_to_7_segment_decoder_3: pin names not known
endmodule

module addr_display (
  input  [15:0] in_1
);

  Hex_Digit_Display #(.decimalPoint("false")) d3 (.value(in_1[15:12]));
  Hex_Digit_Display #(.decimalPoint("false")) d2 (.value(in_1[11:8]));
  Hex_Digit_Display #(.decimalPoint("false")) d1 (.value(in_1[7:4]));
  Hex_Digit_Display #(.decimalPoint("false")) d0 (.value(in_1[3:0]));
endmodule

module gfx_ctr (
  input  CLK,
  output [8:0] H,
  output hsend,
  output hsync,
  output [8:0] V,
  output vsend,
  output vsync
);

  wire and_1_out, and_2_out, and_3_out, and_4_out, and_5_out, and_6_out, and_7_out, and_8_out, and_9_out,
       and_10_out, not_1_out, not_2_out, not_3_out, not_4_out, not_5_out, not_6_out, not_7_out, not_8_out,
       not_9_out, not_10_out, not_11_out, not_12_out, not_13_out, not_14_out, not_15_out, not_16_out;

  Counter #(.max('h1ff), .width(9)) counter_1 (
    .clr(and_1_out), .load(1'b0), .up(1'b1), .count(1'b1), .clk(CLK), .Q(H));  // open: D, carry
  Counter #(.max('h1ff), .width(9)) counter_2 (
    .clr(and_2_out), .load(1'b0), .up(1'b1), .count(and_3_out), .clk(CLK), .Q(V));  // open: D, carry
  and and_1 (and_1_out, H[0], and_3_out);
  and and_2 (and_2_out, V[0], and_4_out);
  not not_1 (not_1_out, H[0]);
  not not_2 (not_2_out, H[1]);
  not not_3 (not_3_out, H[2]);
  not not_4 (not_4_out, H[3]);
  not not_5 (not_5_out, H[4]);
  not not_6 (not_6_out, H[5]);
  not not_7 (not_7_out, H[6]);
  not not_8 (not_8_out, H[7]);
  not not_9 (not_9_out, V[0]);
  not not_10 (not_10_out, V[1]);
  not not_11 (not_11_out, V[2]);
  not not_12 (not_12_out, V[3]);
  not not_13 (not_13_out, V[4]);
  not not_14 (not_14_out, V[5]);
  not not_15 (not_15_out, V[6]);
  not not_16 (not_16_out, V[7]);
  LED h264 (.in(and_3_out));
  and and_3 (and_3_out, not_2_out, not_3_out, H[3], not_5_out, not_6_out, not_7_out, not_8_out, H[8]);
  LED v264 (.in(and_4_out));
  and and_4 (and_4_out, not_10_out, not_11_out, V[3], not_13_out, not_14_out, not_15_out, not_16_out, V[8]);
  LED h242 (.in(and_5_out));
  and and_5 (and_5_out, not_1_out, H[1], not_3_out, not_4_out, H[4], H[5], H[6], H[7]);
  and and_6 (and_6_out, not_9_out, V[1], not_11_out, not_12_out, V[4], V[5], V[6], V[7]);
  LED v242 (.in(and_6_out));
  LED h210 (.in(and_7_out));
  and and_7 (and_7_out, not_1_out, H[1], not_3_out, not_4_out, H[4], not_6_out, H[6], H[7]);
  LED v210 (.in(and_8_out));
  and and_8 (and_8_out, not_9_out, V[1], not_11_out, not_12_out, V[4], not_14_out, V[6], V[7]);
  LED h200 (.in(and_9_out));
  and and_9 (and_9_out, not_1_out, not_2_out, not_3_out, H[3], not_5_out, not_6_out, H[6], H[7]);
  and and_10 (and_10_out, not_9_out, not_10_out, not_11_out, V[3], not_13_out, not_14_out, V[6], V[7]);
  S_R_Flip_Flop #(.trigger("high")) s_r_ff_1 (
    .S(and_3_out), .R(and_9_out), .clk(CLK), .Q(hsend));  // open: reset, Qn, preset
  S_R_Flip_Flop #(.trigger("high")) s_r_ff_2 (
    .S(and_5_out), .R(and_7_out), .clk(CLK), .Q(hsync));  // open: reset, Qn, preset
  LED v200 (.in(and_10_out));
  S_R_Flip_Flop s_r_ff_3 (.S(and_4_out), .R(and_10_out), .clk(CLK), .Q(vsend));  // open: reset, Qn, preset
  S_R_Flip_Flop s_r_ff_4 (.S(and_6_out), .R(and_8_out), .clk(CLK), .Q(vsync));  // open: reset, Qn, preset
endmodule

module gfx_ex (
  input  [7:0] COLOR
);

  wire and_1_out, buffer_1_out, buffer_2_out, buffer_3_out, buffer_4_out, buffer_5_out, buffer_6_out,
       clock_1_out, controlled_buffer_1_out, controlled_buffer_2_out, controlled_buffer_3_out,
       gfx_ctr_1_hsend, gfx_ctr_1_hsync, gfx_ctr_1_vsend, gfx_ctr_1_vsync, or_1_out, or_2_out, or_3_out;

  Clock clock_1 (.out(clock_1_out));
  gfx_ctr gfx_ctr_1 (
    .CLK(clock_1_out), .hsend(gfx_ctr_1_hsend), .hsync(gfx_ctr_1_hsync), .vsend(gfx_ctr_1_vsend),
    .vsync(gfx_ctr_1_vsync));  // open: H, V
  LED HSYNC (.in(gfx_ctr_1_hsync));
  LED VSYNC (.in(gfx_ctr_1_vsync));
  buf buffer_1 (buffer_1_out, COLOR[0]);
  buf buffer_2 (buffer_2_out, COLOR[1]);
  buf buffer_3 (buffer_3_out, COLOR[2]);
  buf buffer_4 (buffer_4_out, COLOR[3]);
  buf buffer_5 (buffer_5_out, COLOR[4]);
  buf buffer_6 (buffer_6_out, COLOR[5]);
  and and_1 (and_1_out, gfx_ctr_1_hsend, gfx_ctr_1_vsend);
  or or_1 (or_1_out, buffer_1_out, buffer_2_out);
  assign controlled_buffer_1_out = and_1_out ? or_1_out : 1'bz;  // Controlled_Buffer controlled_buffer_1
  or or_2 (or_2_out, buffer_3_out, buffer_4_out);
  assign controlled_buffer_2_out = and_1_out ? or_2_out : 1'bz;  // Controlled_Buffer controlled_buffer_2
  or or_3 (or_3_out, buffer_5_out, buffer_6_out);
  assign controlled_buffer_3_out = and_1_out ? or_3_out : 1'bz;  // Controlled_Buffer controlled_buffer_3
  LED R (.in(controlled_buffer_1_out));
  LED G (.in(controlled_buffer_2_out));
  LED B (.in(controlled_buffer_3_out));

  // Notes on the sheet:
  //   1.5kOhm
  //   680Ohm
  //   1.5kOhm
  //   680Ohm
  //   1.5kOhm
  //   680Ohm
  //   Active video
  //   Pretend the BUFFER gates are resisters and the OR gates are wire connections (voltage divider)
endmodule

module icalu (
);

  wire a0, a1, a2, a3, AB0, AB1, AB2, AB3, AB4, AB5, AB6, AB7, AB8, AB9, AB10, AB11, AB12, AB13, AB14, AB15,
       ALU_Q0, ALU_Q1, ALU_Q2, ALU_Q3, ALUB_0, ALUB_1, ALUB_2, ALUB_3, ALUB_4, ALUB_5, ALUB_6, ALUB_7,
       ALUOP_0, ALUOP_1, ALUOP_2, AR_PC, ax0c, ax1c, ax2c, ax3c, BF, c0, c1, c2, c3, C_in, C_out, CF, CLK,
       D0, D1, D2, D3, D4, D5, D6, D7, EF, F_B, F_C, F_E, F_L, F_Q0, F_Q1, F_Q2, F_Q3, F_Q4, F_Q5, F_Q6,
       F_Q7, F_Z, INV_B, INV_Q, LF, LHS_Q0, LHS_Q1, LHS_Q2, LHS_Q3, LHS_Q4, LHS_Q5, LHS_Q6, LHS_Q7,
       multiplexer_1_out, mx_C_in, n7400_1_pin2, n7400_1_pin3, n7400_1_pin6, n7400_1_pin12, n7400_2_pin2,
       n7400_2_pin5, n7402_1_pin8, n7402_1_pin10, n74138_1_pin4, n74138_1_pin5, n74138_1_pin6, n74138_2_pin4,
       n74138_2_pin5, n74138_2_pin6, n74157_1_pin15, n74157_2_pin15, n74157_3_pin15, n74157_4_pin15,
       n74245_1_pin1, n74245_2_pin1, n74245_3_pin1, n74245_5_pin1, n74245_6_pin1, n74245_7_pin1,
       n74245_8_pin1, nadd, nALU_SEL_A, nALU_SEL_B, nALU_SEL_C, nALU_SEL_D, nALU_SEL_F, nALU_SEL_X,
       nALU_SEL_Y, nALU_SEL_Z, nAW_LR, nC_out, ncmp, nDR_F, nDR_LHS, nDR_RHS, nDW_AF, nDW_F, nDW_LHS,
       nDW_RHS, nF_B, nnand, nnor, not_1_out, not_2_out, nsub, op_cmp, op_sub, PCJMP, PCJNZ, RHS_Q0, RHS_Q1,
       RHS_Q2, RHS_Q3, RHS_Q4, RHS_Q5, RHS_Q6, RHS_Q7, sel_z, x0, x1, x2, x3, Z, ZF;

  _74245 #(.ShowInternalStructure("true")) u_74245_1 (
    .pin1(n74245_1_pin1), .pin2(ALUB_0), .pin3(ALUB_1), .pin4(ALUB_2), .pin5(ALUB_3), .pin6(ALUB_4),
    .pin7(ALUB_5), .pin8(ALUB_6), .pin9(ALUB_7), .pin19(nALU_SEL_F), .pin18(F_E), .pin17(F_L), .pin16(F_C),
    .pin15(F_B), .pin14(F_Z), .pin13(F_Q5), .pin12(F_Q6), .pin11(F_Q7));
  _74377 #(.ShowInternalStructure("true")) u_74377_1 (
    .pin1(nDR_F), .pin2(F_E), .pin3(D0), .pin4(D1), .pin5(F_L), .pin6(F_C), .pin7(D2), .pin8(D3), .pin9(F_B),
    .pin19(F_Q7), .pin18(D7), .pin17(D6), .pin16(F_Q6), .pin15(F_Q5), .pin14(D5), .pin13(D4), .pin12(F_Z),
    .pin11(CLK));
  _74245 #(.ShowInternalStructure("true")) u_74245_2 (
    .pin1(n74245_2_pin1), .pin2(F_Q0), .pin3(F_Q1), .pin4(F_Q2), .pin5(F_Q3), .pin6(F_Q4), .pin7(F_Q5),
    .pin8(F_Q6), .pin9(F_Q7), .pin19(nDW_F), .pin18(D0), .pin17(D1), .pin16(D2), .pin15(D3), .pin14(D4),
    .pin13(D5), .pin12(D6), .pin11(D7));
  _74245 #(.ShowInternalStructure("true")) u_74245_3 (
    .pin1(n74245_3_pin1), .pin19(nDW_AF), .pin18(D0), .pin17(D1), .pin16(D2), .pin15(D3), .pin14(D4),
    .pin13(D5), .pin12(D6), .pin11(D7));  // open: pin2, pin3, pin4, pin5, pin6, pin7, pin8, pin9
  _74157 #(.ShowInternalStructure("true")) u_74157_1 (
    .pin1(ncmp), .pin2(nC_out), .pin3(F_L), .pin4(LF), .pin5(Z), .pin6(F_E), .pin7(EF), .pin15(n74157_1_pin15));  // open: pin14, pin13, pin12, pin11, pin10, pin9
  _74157 #(.ShowInternalStructure("true")) u_74157_2 (
    .pin1(sel_z), .pin2(Z), .pin3(F_Z), .pin4(ZF), .pin15(n74157_2_pin15));  // open: pin5, pin6, pin7, pin14, pin13, pin12, pin11, pin10, pin9
  _7402 #(.ShowInternalStructure("true")) u_7402_1 (
    .pin1(INV_Q), .pin2(nnor), .pin3(nnand), .pin4(INV_B), .pin5(nsub), .pin6(ncmp), .pin13(sel_z),
    .pin12(nsub), .pin11(nadd), .pin10(n7402_1_pin10), .pin9(PCJMP), .pin8(n7402_1_pin8));
  _7400 #(.ShowInternalStructure("true")) u_7400_1 (
    .pin1(Z), .pin2(n7400_1_pin2), .pin3(n7400_1_pin3), .pin4(n7400_1_pin3), .pin5(PCJNZ),
    .pin6(n7400_1_pin6), .pin13(n7402_1_pin10), .pin12(n7400_1_pin12), .pin11(AR_PC), .pin10(n7400_1_pin6),
    .pin9(n7400_1_pin6), .pin8(n7402_1_pin8));
  _7400 #(.ShowInternalStructure("true")) u_7400_2 (
    .pin1(C_out), .pin2(n7400_2_pin2), .pin3(nC_out), .pin4(F_B), .pin5(n7400_2_pin5), .pin6(nF_B));  // open: pin13, pin12, pin11, pin10, pin9, pin8
  Multiplexer multiplexer_1 (.in0(F_C), .in1(not_1_out), .out(multiplexer_1_out), .sel(op_sub));
  not not_1 (not_1_out, F_B);
  _74139 u_74139_1 ();  // open: pin1, pin2, pin3, pin4, pin5, pin6, pin7, pin15, pin14, pin13, pin12, pin11, pin10, pin9
  _74139 u_74139_2 ();  // open: pin1, pin2, pin3, pin4, pin5, pin6, pin7, pin15, pin14, pin13, pin12, pin11, pin10, pin9
  _7486 u_7486_1 ();  // open: pin1, pin2, pin3, pin4, pin5, pin6, pin13, pin12, pin11, pin10, pin9, pin8
  _74245 u_74245_4 ();  // open: pin1, pin2, pin3, pin4, pin5, pin6, pin7, pin8, pin9, pin19, pin18, pin17, pin16, pin15, pin14, pin13, pin12, pin11
  _7430 u_7430_1 ();  // open: pin1, pin2, pin3, pin4, pin5, pin6, pin13, pin12, pin11, pin10, pin9, pin8
  not not_2 (not_2_out, op_cmp);
  and and_1 (C_in, not_2_out, multiplexer_1_out);
  _7486 u_7486_2 ();  // open: pin1, pin2, pin3, pin4, pin5, pin6, pin13, pin12, pin11, pin10, pin9, pin8
  _74139 u_74139_3 ();  // open: pin1, pin2, pin3, pin4, pin5, pin6, pin7, pin15, pin14, pin13, pin12, pin11, pin10, pin9
  _74139 u_74139_4 ();  // open: pin1, pin2, pin3, pin4, pin5, pin6, pin7, pin15, pin14, pin13, pin12, pin11, pin10, pin9
  _74138 #(.ShowInternalStructure("true")) u_74138_1 (
    .pin1(ALUOP_0), .pin2(ALUOP_1), .pin3(ALUOP_2), .pin4(n74138_1_pin4), .pin5(n74138_1_pin5),
    .pin6(n74138_1_pin6), .pin15(nadd), .pin14(nsub), .pin12(nnor), .pin10(nnand), .pin9(ncmp));  // open: pin7, pin13, pin11
  _74157 #(.ShowInternalStructure("true")) u_74157_3 (
    .pin1(nadd), .pin2(C_out), .pin3(F_C), .pin4(CF), .pin15(n74157_3_pin15));  // open: pin5, pin6, pin7, pin14, pin13, pin12, pin11, pin10, pin9
  _74157 #(.ShowInternalStructure("true")) u_74157_4 (
    .pin1(nsub), .pin2(F_B), .pin3(nC_out), .pin4(BF), .pin5(F_C), .pin6(nF_B), .pin7(mx_C_in),
    .pin15(n74157_4_pin15));  // open: pin14, pin13, pin12, pin11, pin10, pin9
  _7486 u_7486_3 (
    .pin1(ALUB_0), .pin2(RHS_Q0), .pin3(x0), .pin4(C_in), .pin5(x0), .pin6(ALU_Q0), .pin13(a0), .pin12(ax0c),
    .pin11(c0), .pin10(ALUB_1), .pin9(RHS_Q1), .pin8(x1));
  _7408 u_7408_1 (
    .pin1(x0), .pin2(C_in), .pin3(ax0c), .pin4(ALUB_0), .pin5(RHS_Q0), .pin6(a0), .pin13(ALUB_1),
    .pin12(RHS_Q1), .pin11(a1), .pin10(x1), .pin9(c0), .pin8(ax1c));
  _7486 u_7486_4 (
    .pin1(ALUB_2), .pin2(RHS_Q2), .pin3(x2), .pin4(c1), .pin5(x2), .pin6(ALU_Q2), .pin13(x1), .pin12(c0),
    .pin11(ALU_Q1), .pin10(a1), .pin9(ax1c), .pin8(c1));
  _7408 u_7408_2 (
    .pin1(x2), .pin2(c1), .pin3(ax2c), .pin4(ALUB_2), .pin5(RHS_Q2), .pin6(a2), .pin13(ALUB_3),
    .pin12(RHS_Q3), .pin11(a3), .pin10(x3), .pin9(c2), .pin8(ax3c));
  _7486 u_7486_5 (
    .pin1(a2), .pin2(ax2c), .pin3(c2), .pin4(ALUB_3), .pin5(RHS_Q3), .pin6(x3), .pin13(x3), .pin12(c2),
    .pin11(ALU_Q3), .pin10(a3), .pin9(ax3c), .pin8(c3));
  _7432 u_7432_1 ();  // open: pin1, pin2, pin3, pin4, pin5, pin6, pin13, pin12, pin11, pin10, pin9, pin8
  _7408 u_7408_3 ();  // open: pin1, pin2, pin3, pin4, pin5, pin6, pin13, pin12, pin11, pin10, pin9, pin8
  _7432 u_7432_2 ();  // open: pin1, pin2, pin3, pin4, pin5, pin6, pin13, pin12, pin11, pin10, pin9, pin8
  _7408 u_7408_4 ();  // open: pin1, pin2, pin3, pin4, pin5, pin6, pin13, pin12, pin11, pin10, pin9, pin8
  _7486 u_7486_6 ();  // open: pin1, pin2, pin3, pin4, pin5, pin6, pin13, pin12, pin11, pin10, pin9, pin8
  _7408 u_7408_5 ();  // open: pin1, pin2, pin3, pin4, pin5, pin6, pin13, pin12, pin11, pin10, pin9, pin8
  _7486 u_7486_7 ();  // open: pin1, pin2, pin3, pin4, pin5, pin6, pin13, pin12, pin11, pin10, pin9, pin8
  _7408 u_7408_6 ();  // open: pin1, pin2, pin3, pin4, pin5, pin6, pin13, pin12, pin11, pin10, pin9, pin8
  _7486 u_7486_8 ();  // open: pin1, pin2, pin3, pin4, pin5, pin6, pin13, pin12, pin11, pin10, pin9, pin8
  _74377 u_74377_2 (
    .pin1(nDR_LHS), .pin2(LHS_Q0), .pin3(D0), .pin4(D1), .pin5(LHS_Q1), .pin6(LHS_Q2), .pin7(D2), .pin8(D3),
    .pin9(LHS_Q3), .pin19(LHS_Q7), .pin18(D7), .pin17(D6), .pin16(LHS_Q6), .pin15(LHS_Q5), .pin14(D5),
    .pin13(D4), .pin12(LHS_Q4), .pin11(CLK));
  _74245 u_74245_5 (
    .pin1(n74245_5_pin1), .pin2(LHS_Q0), .pin3(LHS_Q1), .pin4(LHS_Q2), .pin5(LHS_Q3), .pin6(LHS_Q4),
    .pin7(LHS_Q5), .pin8(LHS_Q6), .pin9(LHS_Q7), .pin19(nDW_LHS), .pin18(D0), .pin17(D1), .pin16(D2),
    .pin15(D3), .pin14(D4), .pin13(D5), .pin12(D6), .pin11(D7));
  _74245 u_74245_6 (
    .pin1(n74245_6_pin1), .pin2(LHS_Q0), .pin3(LHS_Q1), .pin4(LHS_Q2), .pin5(LHS_Q3), .pin6(LHS_Q4),
    .pin7(LHS_Q5), .pin8(LHS_Q6), .pin9(LHS_Q7), .pin19(nAW_LR), .pin18(AB0), .pin17(AB1), .pin16(AB2),
    .pin15(AB3), .pin14(AB4), .pin13(AB5), .pin12(AB6), .pin11(AB7));
  _74138 u_74138_2 (
    .pin1(LHS_Q0), .pin2(LHS_Q1), .pin3(LHS_Q2), .pin4(n74138_2_pin4), .pin5(n74138_2_pin5),
    .pin6(n74138_2_pin6), .pin7(nALU_SEL_F), .pin15(nALU_SEL_A), .pin14(nALU_SEL_B), .pin13(nALU_SEL_C),
    .pin12(nALU_SEL_D), .pin11(nALU_SEL_X), .pin10(nALU_SEL_Y), .pin9(nALU_SEL_Z));
  _74245 #(.ShowInternalStructure("true")) u_74245_7 (
    .pin1(n74245_7_pin1), .pin2(RHS_Q0), .pin3(RHS_Q1), .pin4(RHS_Q2), .pin5(RHS_Q3), .pin6(RHS_Q4),
    .pin7(RHS_Q5), .pin8(RHS_Q6), .pin9(RHS_Q7), .pin19(nDW_RHS), .pin18(D0), .pin17(D1), .pin16(D2),
    .pin15(D3), .pin14(D4), .pin13(D5), .pin12(D6), .pin11(D7));
  _74377 #(.ShowInternalStructure("true")) u_74377_3 (
    .pin1(nDR_RHS), .pin2(RHS_Q0), .pin3(D0), .pin4(D1), .pin5(RHS_Q1), .pin6(RHS_Q2), .pin7(D2), .pin8(D3),
    .pin9(RHS_Q3), .pin19(RHS_Q7), .pin18(D7), .pin17(D6), .pin16(RHS_Q6), .pin15(RHS_Q5), .pin14(D5),
    .pin13(D4), .pin12(RHS_Q4), .pin11(CLK));
  _7486 #(.ShowInternalStructure("true")) u_7486_9 (
    .pin1(RHS_Q0), .pin2(INV_B), .pin4(RHS_Q1), .pin5(INV_B), .pin13(RHS_Q4), .pin12(INV_B), .pin10(RHS_Q5),
    .pin9(INV_B));  // open: pin3, pin6, pin11, pin8
  _7486 #(.ShowInternalStructure("true")) u_7486_10 (
    .pin1(RHS_Q2), .pin2(INV_B), .pin4(RHS_Q3), .pin5(INV_B), .pin13(RHS_Q6), .pin12(INV_B), .pin10(RHS_Q7),
    .pin9(INV_B));  // open: pin3, pin6, pin11, pin8
  _74245 #(.ShowInternalStructure("true")) u_74245_8 (
    .pin1(n74245_8_pin1), .pin2(RHS_Q0), .pin3(RHS_Q1), .pin4(RHS_Q2), .pin5(RHS_Q3), .pin6(RHS_Q4),
    .pin7(RHS_Q5), .pin8(RHS_Q6), .pin9(RHS_Q7), .pin19(nAW_LR), .pin18(AB8), .pin17(AB9), .pin16(AB10),
    .pin15(AB11), .pin14(AB12), .pin13(AB13), .pin12(AB14), .pin11(AB15));
  // also tied to GND on the sheet: {n74245_1_pin1, n74157_1_pin15, n74157_2_pin15, n74138_1_pin4, n74138_1_pin5, n74157_3_pin15, n74157_4_pin15, n74138_2_pin4, n74138_2_pin5, C_out, Z}
  // also tied to VCC on the sheet: {n74245_3_pin1, n7400_1_pin2, n7400_2_pin2, n7400_2_pin5, n74245_2_pin1, n7400_1_pin12, n74138_1_pin6, n74245_7_pin1, n74245_8_pin1, n74245_5_pin1, n74245_6_pin1, n74138_2_pin6}

  // Notes on the sheet:
  //   These are 74253s  ->
  //   These are 74253s  ->
  //   INV_Q (LOW)
  //   74682  ->
  //   == 0
  //   INV_Q (HIGH)
  //   4 bit adder / logic
  //   LHS
  //   RHS
endmodule
